# Fritzing sketch diagrama (saved by Fritzing 0.9.2b)
breadboards: 1

parts:
  J1 = Basic Servo
  J2 = Basic Servo
  Componente1 = Arduino Nano (Rev3.0) (ICSP)

nets:
  GND: J1.gnd, J2.gnd, Componente1.GND
  VCC: J1.vcc, J2.vcc, Componente1.5V
  N1: J1.pulse, Componente1.D11/MOSI
  N2: J2.pulse, Componente1.D10
